# Fritzing sketch connectiondiagram (saved by Fritzing 0.9.1b)
breadboards: 1

parts:
  Part1 = Arduino Uno (Rev3)
  S1 = Pushbutton [package="[THT]"]
  S2 = Pushbutton [package="[THT]"]
  S3 = Pushbutton [package="[THT]"]
  R1 = Resistor [tolerance=±5% resistance=100 package=THT]
  R2 = Resistor [tolerance=±5% resistance=100 package=THT]
  R3 = Resistor [tolerance=±5% resistance=100 package=THT]
  R4 = Resistor [tolerance=±5% resistance=10k package=THT]
  R6 = Resistor [tolerance=±5% resistance=10k package=THT]
  R5 = Resistor [tolerance=±5% resistance=10k package=THT]
  U1 = Voltage Regulator - 5V [package="TO220 [THT]"]
  VCC1 = Battery block 9V
  D2 = Rectifier Diode [part_number=1N4001 package="300 mil [THT]"]
  Part2 = Bluetooth Module Breakout - Roving Networks (RN-41)

nets:
  N1: Part1.D13/SCK, U1.output_voltage
  GND: Part1.GND, S1.Pin_3, S1.Pin_4, S2.Pin_3, S2.Pin_4, S3.Pin_3, S3.Pin_4, Part2.GND
  N2: Part1.D0/RX, Part2.UARTRX
  N3: Part1.D1/TX, Part2.UARTTX
  N4: Part1.D2, R2.Pin_1
  N5: Part1.D3_PWM, R3.Pin_1
  N6: Part1.D4, R1.Pin_1
  3V3: Part1.3V3, Part2.VCC
  N7: Part1.5V, R4.Pin_0, R6.Pin_0, R5.Pin_0
  N8: S1.Pin_1, S1.Pin_2, R3.Pin_0, R5.Pin_1
  N9: S2.Pin_1, S2.Pin_2, R1.Pin_0, R4.Pin_1
  N10: S3.Pin_1, S3.Pin_2, R2.Pin_0, R6.Pin_1
  N11: U1.input_voltage, VCC1.+
  N12: U1.GND, D2.cathode
  N13: VCC1.-, D2.anode

notes:
  DoorLock
