# Fritzing sketch displaysketch (saved by Fritzing 0.9.1b)
breadboards: 1

parts:
  Part1 = Arduino Uno (Rev3)
  LCD1 = LCD screen
  LED1 = LED - 5mm [color="Red (633nm)" package="5 mm [THT]"]
  Green_LED2 = LED - 5mm [color="Red (633nm)" package="5 mm [THT]"]
  R7 = Resistor [tolerance=±5% resistance=1k package=THT]
  R8 = Resistor [tolerance=±5% resistance=1k package=THT]

nets:
  N1: Part1.D8, LCD1.DB4
  N2: Part1.D9_PWM, R7.Pin_1
  N3: Part1.D10_PWM/SS, R8.Pin_1
  N4: Part1.D11_PWM/MOSI, LCD1.E
  N5: Part1.D12/MISO, LCD1.RS
  GND: Part1.GND, LCD1.VSS, LCD1.V0, LCD1.R/W, LCD1.LED-
  N6: Part1.D5_PWM, LCD1.DB7
  N7: Part1.D6_PWM, LCD1.DB6
  N8: Part1.D7, LCD1.DB5
  5V: Part1.5V, LCD1.VDD, LCD1.LED+, LED1.cathode, Green_LED2.cathode
  N9: LED1.anode, R8.Pin_0
  N10: Green_LED2.anode, R7.Pin_0
