# Fritzing sketch finalsketch (saved by Fritzing 0.9.1b)
breadboards: 1

parts:
  Part1 = Arduino Uno (Rev3)
  S1 = Pushbutton [package="[THT]"]
  S2 = Pushbutton [package="[THT]"]
  S3 = Pushbutton [package="[THT]"]
  R1 = Resistor [tolerance=±5% resistance=100 package=THT]
  R2 = Resistor [tolerance=±5% resistance=100 package=THT]
  R3 = Resistor [tolerance=±5% resistance=100 package=THT]
  R4 = Resistor [tolerance=±5% resistance=10k package=THT]
  R6 = Resistor [tolerance=±5% resistance=10k package=THT]
  R5 = Resistor [tolerance=±5% resistance=10k package=THT]
  U1 = Voltage Regulator - 5V [package="TO220 [THT]"]
  VCC1 = Battery block 9V
  D2 = Rectifier Diode [part_number=1N4001 package="300 mil [THT]"]
  Part2 = Bluetooth Module Breakout - Roving Networks (RN-41)
  LED1 = RGB LED (com. cathode, rgb) [package="5 mm [THT]"]
  R7 = Resistor [tolerance=±5% resistance=200 package=THT]
  R8 = Resistor [tolerance=±5% resistance=200 package=THT]
  R9 = Resistor [tolerance=±5% resistance=200 package=THT]

nets:
  N1: Part1.D9_PWM, U1.input_voltage
  N2: Part1.D11_PWM/MOSI, R9.Pin_0
  N3: Part1.D12/MISO, R8.Pin_0
  N4: Part1.D13/SCK, R7.Pin_0
  GND: Part1.GND, S1.Pin_3, S1.Pin_4, S2.Pin_3, S2.Pin_4, S3.Pin_3, S3.Pin_4, U1.output_voltage, VCC1.-, D2.anode, Part2.GND
  N5: Part1.D0/RX, Part2.UARTRX
  N6: Part1.D1/TX, Part2.UARTTX
  N7: Part1.D2, R2.Pin_1
  N8: Part1.D3_PWM, R3.Pin_1
  N9: Part1.D4, R1.Pin_1
  3V3: Part1.3V3, Part2.VCC
  N10: Part1.5V, R4.Pin_0, R6.Pin_0, R5.Pin_0
  N11: S1.Pin_1, S1.Pin_2, R3.Pin_0, R5.Pin_1
  N12: S2.Pin_1, S2.Pin_2, R1.Pin_0, R4.Pin_1
  N13: S3.Pin_1, S3.Pin_2, R2.Pin_0, R6.Pin_1
  N14: U1.GND, D2.cathode
  N15: LED1.red_anode, R7.Pin_1
  N16: LED1.green_anode, R8.Pin_1
  N17: LED1.blue_anode, R9.Pin_1

notes:
  DoorLock
