# Fritzing sketch projectsketch (saved by Fritzing 0.9.1b)
breadboards: 1

parts:
  Part1 = Arduino Uno (Rev3)
  S1 = Pushbutton [package="[THT]"]
  S2 = Pushbutton [package="[THT]"]
  S3 = Pushbutton [package="[THT]"]
  R1 = Resistor [tolerance=±5% resistance=100 package=THT]
  R2 = Resistor [tolerance=±5% resistance=100 package=THT]
  R3 = Resistor [tolerance=±5% resistance=100 package=THT]
  R4 = Resistor [tolerance=±5% resistance=10k package=THT]
  R6 = Resistor [tolerance=±5% resistance=10k package=THT]
  R5 = Resistor [tolerance=±5% resistance=10k package=THT]
  LCD1 = LCD screen  # not connected
  U1 = Voltage Regulator - 5V [package="TO220 [THT]"]
  D1 = Rectifier Diode [part_number=1N4001 package="300 mil [THT]"]
  VCC1 = Battery block 9V  # not connected

nets:
  N1: Part1.GND, S1.Pin_3, S1.Pin_4, S2.Pin_3, S2.Pin_4, S3.Pin_3, S3.Pin_4
  N2: Part1.D1/TX, R2.Pin_1
  N3: Part1.D2, R3.Pin_1
  N4: Part1.D3_PWM, R1.Pin_1
  N5: Part1.5V, R4.Pin_0, R6.Pin_0, R5.Pin_0, D1.cathode
  N6: S1.Pin_1, S1.Pin_2, R3.Pin_0, R5.Pin_1
  N7: S2.Pin_1, S2.Pin_2, R1.Pin_0, R4.Pin_1
  N8: S3.Pin_1, S3.Pin_2, R2.Pin_0, R6.Pin_1
  N9: U1.output_voltage, D1.anode
