# Fritzing sketch projectsketch1 (saved by Fritzing 0.9.1b)
breadboards: 1

parts:
  Part1 = Arduino Uno (Rev3)
  S1 = Pushbutton [package="[THT]"]
  S2 = Pushbutton [package="[THT]"]
  S3 = Pushbutton [package="[THT]"]
  R1 = Resistor [tolerance=±5% resistance=100 package=THT]
  R2 = Resistor [tolerance=±5% resistance=100 package=THT]
  R3 = Resistor [tolerance=±5% resistance=100 package=THT]
  R4 = Resistor [tolerance=±5% resistance=10k package=THT]
  R6 = Resistor [tolerance=±5% resistance=10k package=THT]
  R5 = Resistor [tolerance=±5% resistance=10k package=THT]
  LCD1 = LCD screen
  U1 = Voltage Regulator - 5V [package="TO220 [THT]"]
  VCC1 = Battery block 9V
  D2 = Rectifier Diode [part_number=1N4001 package="300 mil [THT]"]
  Part2 = Bluetooth Module Breakout - Roving Networks (RN-41)
  LED1 = LED - 5mm [color="Red (633nm)" package="5 mm [THT]"]
  Green_LED2 = LED - 5mm [color="Red (633nm)" package="5 mm [THT]"]
  R7 = Resistor [tolerance=±5% resistance=1k package=THT]
  R8 = Resistor [tolerance=±5% resistance=1k package=THT]

nets:
  N1: Part1.D8, LCD1.DB4
  N2: Part1.D9_PWM, R7.Pin_1
  N3: Part1.D10_PWM/SS, R8.Pin_1
  N4: Part1.D11_PWM/MOSI, LCD1.E
  N5: Part1.D12/MISO, LCD1.RS
  N6: Part1.D13/SCK, U1.output_voltage
  GND: Part1.GND, S1.Pin_3, S1.Pin_4, S2.Pin_3, S2.Pin_4, S3.Pin_3, S3.Pin_4, LCD1.VSS, LCD1.V0, LCD1.R/W, LCD1.LED-, Part2.GND
  N7: Part1.D0/RX, Part2.UARTRX
  N8: Part1.D1/TX, Part2.UARTTX
  N9: Part1.D2, R2.Pin_1
  N10: Part1.D3_PWM, R3.Pin_1
  N11: Part1.D4, R1.Pin_1
  N12: Part1.D5_PWM, LCD1.DB7
  N13: Part1.D6_PWM, LCD1.DB6
  N14: Part1.D7, LCD1.DB5
  3V3: Part1.3V3, Part2.VCC
  5V: Part1.5V, R4.Pin_0, R6.Pin_0, R5.Pin_0, LCD1.VDD, LCD1.LED+, LED1.cathode, Green_LED2.anode
  N15: S1.Pin_1, S1.Pin_2, R3.Pin_0, R5.Pin_1
  N16: S2.Pin_1, S2.Pin_2, R1.Pin_0, R4.Pin_1
  N17: S3.Pin_1, S3.Pin_2, R2.Pin_0, R6.Pin_1
  N18: U1.input_voltage, VCC1.+
  N19: U1.GND, D2.cathode
  N20: VCC1.-, D2.anode
  N21: LED1.anode, R8.Pin_0
  N22: Green_LED2.cathode, R7.Pin_0

notes:
  DoorLock
